// Logisim project processador.circ as structural Verilog: 18 circuits, main circuit main
module main (
  input  N3,
  input  N2,
  input  N1,
  input  N0,
  input  LOAD_IN
);

  wire clock_1_out, CY_carry_in, ULA_c_out, undriven_2, undriven_7, undriven_8, undriven_10, undriven_11,
       undriven_12, undriven_13, undriven_14, undriven_15, undriven_16;
  wire [3:0] ACC_acc_out, adder_2_out, banco_de_registradores_ula_a, banco_de_registradores_ula_b,
       entrada_n_1_n, memoria_de_dados_1_data_out, multiplexer_1_out, multiplexer_2_out, multiplexer_3_out,
       multiplexer_4_out, multiplexer_5_out, multiplexer_6_out, PC_4, PC_pc, ULA, undriven, undriven_3,
       undriven_4, undriven_5, undriven_6, undriven_9;

  Adder #(.width(4)) adder_1 (.a(PC_pc), .b(4'b0100), .out(PC_4));  // open: cin, cout
  Adder #(.width(4)) adder_2 (.a(PC_pc), .b(undriven), .out(adder_2_out));  // open: cin, cout
  Multiplexer #(.select(2), .width(4)) multiplexer_1 (
    .in1(PC_4), .in2(adder_2_out), .in3(ULA), .out(multiplexer_1_out));  // open: in0, sel, en
  Clock clock_1 (.out(clock_1_out));
  PC PC (.PC_In(multiplexer_1_out), .Seletor_PC(undriven_2), .clk(clock_1_out), .PC(PC_pc));
  banco_de_registradores banco_de_registradores (
    .RD(undriven_4), .Resultado(multiplexer_6_out), .clk(clock_1_out), .WriteEn(undriven_7),
    .RG1(undriven_5), .RG2(undriven_6), .ULA_A(banco_de_registradores_ula_a),
    .ULA_B(banco_de_registradores_ula_b));
  ACC ACC (.ACC_In(ULA), .clk(clock_1_out), .ACC_Out(ACC_acc_out));  // open: ACC_Load
  CY CY (.Carry_ULA(ULA_c_out), .clk(clock_1_out), .Carry_Load(undriven_8), .Carry_In(CY_carry_in));
  Multiplexer #(.width(4)) multiplexer_2 (
    .in0(banco_de_registradores_ula_a), .in1(ACC_acc_out), .out(multiplexer_2_out));  // open: sel, en
  Multiplexer #(.select(2), .width(4)) multiplexer_3 (
    .in1(banco_de_registradores_ula_b), .in2(undriven_9), .in3(ACC_acc_out), .out(multiplexer_3_out));  // open: in0, sel, en
  ULA u_ULA (
    .A(multiplexer_2_out), .B(multiplexer_3_out), .C_In(CY_carry_in), .S2(undriven_10), .S1(undriven_11),
    .S0(undriven_12), .SAIDA(ULA), .C_out(ULA_c_out));  // open: OVERFLOW
  Multiplexer #(.width(4)) multiplexer_4 (
    .in0(ULA), .in1(banco_de_registradores_ula_a), .out(multiplexer_4_out), .en(undriven_13));  // open: sel
  Multiplexer #(.width(4)) multiplexer_5 (
    .in0(undriven_3), .in1(banco_de_registradores_ula_b), .out(multiplexer_5_out), .en(undriven_14));  // open: sel
  memoria_de_dados memoria_de_dados_1 (
    .\endereço (multiplexer_5_out), .data_in(multiplexer_4_out), .store(undriven_15), .load(undriven_16),
    .clock(clock_1_out), .data_out(memoria_de_dados_1_data_out));
  Entrada_N entrada_n_1 (.clk(clock_1_out), .N3(N3), .N2(N2), .N1(N1), .N0(N0), .LOAD_IN(LOAD_IN), .N(entrada_n_1_n));
  Multiplexer #(.select(2), .width(4)) multiplexer_6 (
    .in0(ULA), .in1(memoria_de_dados_1_data_out), .in2(entrada_n_1_n), .in3(PC_4), .out(multiplexer_6_out));  // open: sel, en

  // Notes on the sheet:
  //   PC_SELECT
  //   Instrução
  //   Instrução
  //   Imediato
  //   Shifter e extensor??
  //   Centro de controle
endmodule

module banco_de_registradores (
  input  [3:0] RD,
  input  [3:0] Resultado,
  input  clk,
  input  WriteEn,
  input  [3:0] RG1,
  input  [3:0] RG2,
  output [3:0] ULA_A,
  output [3:0] ULA_B
);

  wire decoder_1_out0, decoder_1_out1, decoder_1_out2, decoder_1_out3, decoder_1_out4, decoder_1_out5,
       decoder_1_out6, decoder_1_out7, decoder_1_out8, decoder_1_out9, decoder_1_out10, decoder_1_out11,
       decoder_1_out12, decoder_1_out13, decoder_1_out14, decoder_1_out15;
  wire [3:0] registradores_1_r0, registradores_1_r1, registradores_1_r2, registradores_1_r3,
       registradores_1_r4, registradores_1_r5, registradores_1_r6, registradores_1_r7, registradores_1_r8,
       registradores_1_r9, registradores_1_r10, registradores_1_r11, registradores_1_r12,
       registradores_1_r13, registradores_1_ra_2, registradores_1_sp_2;

  Decoder #(.select(4)) decoder_1 (
    .out0(decoder_1_out0), .out1(decoder_1_out1), .out2(decoder_1_out2), .out3(decoder_1_out3),
    .out4(decoder_1_out4), .out5(decoder_1_out5), .out6(decoder_1_out6), .out7(decoder_1_out7),
    .out8(decoder_1_out8), .out9(decoder_1_out9), .out10(decoder_1_out10), .out11(decoder_1_out11),
    .out12(decoder_1_out12), .out13(decoder_1_out13), .out14(decoder_1_out14), .out15(decoder_1_out15),
    .sel(RD));  // open: en
  registradores registradores_1 (
    .Load(Resultado), .en0(decoder_1_out0), .en1(decoder_1_out1), .en2(decoder_1_out2), .en3(decoder_1_out3),
    .en4(decoder_1_out4), .en5(decoder_1_out5), .en6(decoder_1_out6), .en7(decoder_1_out7),
    .en8(decoder_1_out8), .en9(decoder_1_out9), .en10(decoder_1_out10), .en11(decoder_1_out11),
    .en12(decoder_1_out12), .en13(decoder_1_out13), .SP(decoder_1_out14), .RA(decoder_1_out15),
    .WriteEnable(WriteEn), .clk(clk), .R0(registradores_1_r0), .R1(registradores_1_r1),
    .R2(registradores_1_r2), .R3(registradores_1_r3), .R4(registradores_1_r4), .R5(registradores_1_r5),
    .R6(registradores_1_r6), .R7(registradores_1_r7), .R8(registradores_1_r8), .R9(registradores_1_r9),
    .R10(registradores_1_r10), .R11(registradores_1_r11), .R12(registradores_1_r12),
    .R13(registradores_1_r13), .SP_2(registradores_1_sp_2), .RA_2(registradores_1_ra_2));
  Multiplexer #(.select(4), .width(4)) multiplexer_1 (
    .in0(registradores_1_r0), .in1(registradores_1_r1), .in2(registradores_1_r2), .in3(registradores_1_r3),
    .in4(registradores_1_r4), .in5(registradores_1_r5), .in6(registradores_1_r6), .in7(registradores_1_r7),
    .in8(registradores_1_r8), .in9(registradores_1_r9), .in10(registradores_1_r10),
    .in11(registradores_1_r11), .in12(registradores_1_r12), .in13(registradores_1_r13),
    .in14(registradores_1_sp_2), .in15(registradores_1_ra_2), .out(ULA_A), .sel(RG1));  // open: en
  Multiplexer #(.select(4), .width(4)) multiplexer_2 (
    .in0(registradores_1_r0), .in1(registradores_1_r1), .in2(registradores_1_r2), .in3(registradores_1_r3),
    .in4(registradores_1_r4), .in5(registradores_1_r5), .in6(registradores_1_r6), .in7(registradores_1_r7),
    .in8(registradores_1_r8), .in9(registradores_1_r9), .in10(registradores_1_r10),
    .in11(registradores_1_r11), .in12(registradores_1_r12), .in13(registradores_1_r13),
    .in14(registradores_1_sp_2), .in15(registradores_1_ra_2), .out(ULA_B), .sel(RG2));  // open: en
endmodule

module registradores (
  input  [3:0] Load,
  input  en0,
  input  en1,
  input  en2,
  input  en3,
  input  en4,
  input  en5,
  input  en6,
  input  en7,
  input  en8,
  input  en9,
  input  en10,
  input  en11,
  input  en12,
  input  en13,
  input  SP,
  input  RA,
  input  WriteEnable,
  input  clk,
  output [3:0] R0,
  output [3:0] R1,
  output [3:0] R2,
  output [3:0] R3,
  output [3:0] R4,
  output [3:0] R5,
  output [3:0] R6,
  output [3:0] R7,
  output [3:0] R8,
  output [3:0] R9,
  output [3:0] R10,
  output [3:0] R11,
  output [3:0] R12,
  output [3:0] R13,
  output [3:0] SP_2,
  output [3:0] RA_2
);

  wire and_1_out, and_2_out, and_3_out, and_4_out, and_5_out, and_6_out, and_7_out, and_8_out, and_9_out,
       and_10_out, and_11_out, and_12_out, and_13_out, and_14_out, and_15_out, and_16_out;

  and and_1 (and_1_out, en0, WriteEnable);
  and and_2 (and_2_out, en1, WriteEnable);
  and and_3 (and_3_out, en2, WriteEnable);
  and and_4 (and_4_out, en3, WriteEnable);
  and and_5 (and_5_out, en4, WriteEnable);
  and and_6 (and_6_out, en5, WriteEnable);
  and and_7 (and_7_out, en6, WriteEnable);
  and and_8 (and_8_out, en7, WriteEnable);
  and and_9 (and_9_out, en8, WriteEnable);
  and and_10 (and_10_out, en9, WriteEnable);
  and and_11 (and_11_out, en10, WriteEnable);
  and and_12 (and_12_out, en11, WriteEnable);
  and and_13 (and_13_out, en12, WriteEnable);
  and and_14 (and_14_out, en13, WriteEnable);
  and and_15 (and_15_out, SP, WriteEnable);
  and and_16 (and_16_out, RA, WriteEnable);
  Register #(.width(4)) u_R0 (.D(Load), .en(and_1_out), .Q(R0), .clk(clk));  // open: clr
  Register #(.width(4)) u_R1 (.D(Load), .en(and_2_out), .Q(R1), .clk(clk));  // open: clr
  Register #(.width(4)) u_R2 (.D(Load), .en(and_3_out), .Q(R2), .clk(clk));  // open: clr
  Register #(.width(4)) u_R3 (.D(Load), .en(and_4_out), .Q(R3), .clk(clk));  // open: clr
  Register #(.width(4)) u_R4 (.D(Load), .en(and_5_out), .Q(R4), .clk(clk));  // open: clr
  Register #(.width(4)) u_R5 (.D(Load), .en(and_6_out), .Q(R5), .clk(clk));  // open: clr
  Register #(.width(4)) u_R6 (.D(Load), .en(and_7_out), .Q(R6), .clk(clk));  // open: clr
  Register #(.width(4)) u_R7 (.D(Load), .en(and_8_out), .Q(R7), .clk(clk));  // open: clr
  Register #(.width(4)) u_R8 (.D(Load), .en(and_9_out), .Q(R8), .clk(clk));  // open: clr
  Register #(.width(4)) u_R9 (.D(Load), .en(and_10_out), .Q(R9), .clk(clk));  // open: clr
  Register #(.width(4)) u_R10 (.D(Load), .en(and_11_out), .Q(R10), .clk(clk));  // open: clr
  Register #(.width(4)) u_R11 (.D(Load), .en(and_12_out), .Q(R11), .clk(clk));  // open: clr
  Register #(.width(4)) u_R12 (.D(Load), .en(and_13_out), .Q(R12), .clk(clk));  // open: clr
  Register #(.width(4)) u_R13 (.D(Load), .en(and_14_out), .Q(R13), .clk(clk));  // open: clr
  Register #(.width(4)) u_SP (.D(Load), .en(and_15_out), .Q(SP_2), .clk(clk));  // open: clr
  Register #(.width(4)) u_RA (.D(Load), .en(and_16_out), .Q(RA_2), .clk(clk));  // open: clr
endmodule

module ULA (
  input  [3:0] A,
  input  [3:0] B,
  input  C_In,
  input  S2,
  input  S1,
  input  S0,
  output [3:0] SAIDA,
  output C_out,
  output OVERFLOW
);

  wire ula_celula_1bit_1_c_out, ula_celula_1bit_2_c_out, ula_celula_1bit_3_c_out, ula_celula_1bit_4_c_out;

  ULA_celula_1bit ula_celula_1bit_1 (
    .A(A[3]), .B(B[3]), .C_in(ula_celula_1bit_2_c_out), .OUT_RESULT(SAIDA[3]), .SEL_OP({S2, S1, S0}),
    .C_out(ula_celula_1bit_1_c_out));
  // overflow overflow_1: pin names not known; wires that end beside it: A[3], B[3], SAIDA[3], ula_celula_1bit_1_c_out, {S2, S1, S0}, OVERFLOW
  ULA_celula_1bit ula_celula_1bit_2 (
    .A(A[2]), .B(B[2]), .C_in(ula_celula_1bit_3_c_out), .OUT_RESULT(SAIDA[2]), .SEL_OP({S2, S1, S0}),
    .C_out(ula_celula_1bit_2_c_out));
  ULA_celula_1bit ula_celula_1bit_3 (
    .A(A[1]), .B(B[1]), .C_in(ula_celula_1bit_4_c_out), .OUT_RESULT(SAIDA[1]), .SEL_OP({S2, S1, S0}),
    .C_out(ula_celula_1bit_3_c_out));
  ULA_celula_1bit ula_celula_1bit_4 (
    .A(A[0]), .B(B[0]), .C_in(C_In), .OUT_RESULT(SAIDA[0]), .SEL_OP({S2, S1, S0}),
    .C_out(ula_celula_1bit_4_c_out));
  and AND (C_out, ula_celula_1bit_1_c_out, ~S2);  // AND_Gate

  // Notes on the sheet:
  //   S2    S1   S0
  //   0      0      0        CLEAR  
  //   0      0      1          NAND
  //   0      1      0          A  - B
  //   0      1      1          A + B
  //   1      0      0         A xor B 
  //   1      0      1         A or B
  //   1      1      0        A and B
  //   1      1      1       PRESET
  //   Tabela de Operaçoes
  //   OPERAÇAO
endmodule

module ULA_celula_1bit (
  input  A,
  input  B,
  input  C_in,
  input  [2:0] SEL_OP,
  output OUT_RESULT,
  output C_out
);

  wire adder_1_cout, adder_1_out, AND_2_out, AND_out, clear_1_out_3, NAND_out, OR_out, preset_1_out_3,
       subtractor_1_bout, subtractor_1_out, XOR_out;

  clear clear_1 (.in_1(A), .in_2(B), .out_3(clear_1_out_3));
  nand NAND (NAND_out, A, B);
  Adder #(.width(1)) adder_1 (.a(A), .b(B), .out(adder_1_out), .cin(C_in), .cout(adder_1_cout));
  Subtractor #(.width(1)) subtractor_1 (.a(A), .b(B), .out(subtractor_1_out), .bin(C_in), .bout(subtractor_1_bout));
  xor XOR (XOR_out, A, B);
  or OR (OR_out, A, B);
  and AND (AND_out, A, B);
  preset preset_1 (.in_1(A), .in_2(B), .out_3(preset_1_out_3));
  Multiplexer #(.select(3), .enable("false")) multiplexer_1 (
    .in0(clear_1_out_3), .in1(NAND_out), .in2(adder_1_out), .in3(subtractor_1_out), .in4(XOR_out),
    .in5(OR_out), .in6(AND_out), .in7(preset_1_out_3), .out(OUT_RESULT), .sel(SEL_OP));
  and AND_2 (AND_2_out, ~SEL_OP[2], SEL_OP[1], ~SEL_OP[0]);  // AND_Gate
  Multiplexer #(.enable("false")) multiplexer_2 (
    .in0(adder_1_cout), .in1(subtractor_1_bout), .out(C_out), .sel(AND_2_out));
endmodule

module preset (
  input  in_1,
  input  in_2,
  output out_3
);


  assign out_3 = 1'b1;
endmodule

module clear (
  input  in_1,
  input  in_2,
  output out_3
);


  assign out_3 = 1'b0;
endmodule

module overflow (
  input  A,
  input  B,
  input  S,
  input  C_IN,
  input  [2:0] SELETOR,
  output OVERFLOW,
  output OVERFLOW_2
);

  wire AND_3_out, AND_4_out, AND_out, OR_out, undriven;

  and AND (AND_out, SELETOR[0], SELETOR[1], ~undriven);  // AND_Gate
  and AND_2 (AND_out, SELETOR[0], SELETOR[1], ~undriven);  // AND_Gate
  and AND_3 (AND_3_out, ~A, S, ~B);  // AND_Gate
  and AND_4 (AND_4_out, A, ~S, B);  // AND_Gate
  and AND_5 (AND_4_out, A, ~S, B);  // AND_Gate
  or OR (OR_out, AND_3_out, AND_4_out);
  Multiplexer #(.enable("false")) multiplexer_1 (.in0(OR_out), .in1(C_IN), .out(OVERFLOW), .sel(AND_out));
  Multiplexer #(.enable("false")) multiplexer_2 (.in0(OR_out), .in1(C_IN), .out(OVERFLOW), .sel(AND_out));

  assign OVERFLOW_2 = OVERFLOW;
endmodule

module memoria_de_dados (
  input  [3:0] \endereço ,
  input  [3:0] data_in,
  input  store,
  input  load,
  input  clock,
  output [3:0] data_out
);

  RAM #(.addrWidth(4), .dataWidth(4), .bus("separate")) ram_1 (
    .addr(\endereço ), .din(data_in), .data(data_out), .str(store), .clk(clock), .ld(load));  // open: sel, clr
endmodule

module PC (
  input  [3:0] PC_In,
  input  Seletor_PC,
  input  clk,
  output [3:0] PC
);

  wire [3:0] adder_1_out, multiplexer_1_out;

  Adder #(.width(4)) adder_1 (.a(PC), .b(4'b0001), .out(adder_1_out));  // open: cin, cout
  Multiplexer #(.width(4)) multiplexer_1 (
    .in0(adder_1_out), .in1(PC_In), .out(multiplexer_1_out), .sel(Seletor_PC));  // open: en
  Register #(.width(4)) u_PC (.D(multiplexer_1_out), .Q(PC), .clk(clk));  // open: en, clr

  // Notes on the sheet:
  //   Fazer com que o CC envie 1 ou 2??
endmodule

module ACC (
  input  [3:0] ACC_In,
  input  clk,
  input  ACC_Load,
  output [3:0] ACC_Out
);

  Register #(.width(4)) register_1 (.D(ACC_In), .en(ACC_Load), .Q(ACC_Out), .clk(clk));  // open: clr
endmodule

module CY (
  input  Carry_ULA,
  input  clk,
  input  Carry_Load,
  output Carry_In
);

  Register #(.width(1)) register_1 (.D(Carry_ULA), .en(Carry_Load), .Q(Carry_In), .clk(clk));  // open: clr
endmodule

module Entrada_N (
  input  clk,
  input  N3,
  input  N2,
  input  N1,
  input  N0,
  input  LOAD_IN,
  output [3:0] N
);

  Register #(.width(4)) register_1 (.D({N3, N2, N1, N0}), .en(LOAD_IN), .Q(N), .clk(clk));  // open: clr

  // Notes on the sheet:
  //   Fazer negócio de guardar clique
endmodule

module i_4004 (
);

  wire clock_1_out, undriven_2, undriven_3, undriven_5, undriven_6, undriven_7, undriven_8, undriven_9,
       undriven_10, undriven_11, undriven_12;
  wire [1:0] undriven;
  wire [3:0] ACC_Out, banco_de_registradores_1_register_out, memoria_de_dados_1_data_out, multiplexer_1_out,
       multiplexer_2_out, ula_1_saida, undriven_4;

  Clock clock_1 (.out(clock_1_out));
  Multiplexer #(.select(2), .width(4)) multiplexer_1 (
    .in0(undriven_4), .in1(banco_de_registradores_1_register_out), .in2(memoria_de_dados_1_data_out),
    .in3(ula_1_saida), .out(multiplexer_1_out), .sel(undriven), .en(undriven_2));
  ACC acc_1 (.ACC_In(multiplexer_1_out), .clk(clock_1_out), .ACC_Load(undriven_3), .ACC_Out(ACC_Out));
  Multiplexer #(.width(4)) multiplexer_2 (
    .in0(undriven_4), .in1(banco_de_registradores_1_register_out), .out(multiplexer_2_out), .sel(undriven_5),
    .en(undriven_6));
  CY cy_1 ();  // open: Carry_ULA, clk, Carry_Load, Carry_In
  ULA ula_1 (
    .A(ACC_Out), .B(multiplexer_2_out), .S2(undriven_7), .S1(undriven_8), .S0(undriven_9), .SAIDA(ula_1_saida));  // open: C_In, C_out, OVERFLOW
  Timing_and_Control timing_and_control_1 ();  // open: Imediato, Seletor_PC, PC_Load, clk, PC
  memoria_de_dados memoria_de_dados_1 (
    .\endereço (banco_de_registradores_1_register_out), .data_in(ACC_Out), .store(undriven_10),
    .load(undriven_11), .clock(clock_1_out), .data_out(memoria_de_dados_1_data_out));
  Banco_de_Registradores banco_de_registradores_1 (
    .RD(undriven_4), .Load(ACC_Out), .clk(clock_1_out), .RegWrite(undriven_12), .r1_ad(undriven_4),
    .Register_Out(banco_de_registradores_1_register_out));

  // Notes on the sheet:
  //   TEMPO + UC
  //   imediato
  //   IR
  //   FSM
  //   Incrementa SP
endmodule

module Banco_de_Registradores (
  input  [3:0] RD,
  input  [3:0] Load,
  input  clk,
  input  RegWrite,
  input  [3:0] r1_ad,
  output [3:0] Register_Out
);

  wire decoder_1_out0, decoder_1_out1, decoder_1_out2, decoder_1_out3, decoder_1_out4, decoder_1_out5,
       decoder_1_out6, decoder_1_out7, decoder_1_out8, decoder_1_out9, decoder_1_out10, decoder_1_out11,
       decoder_1_out12, decoder_1_out13, decoder_1_out14, decoder_1_out15;
  wire [3:0] registradores_1_r0, registradores_1_r1, registradores_1_r2, registradores_1_r3,
       registradores_1_r4, registradores_1_r5, registradores_1_r6, registradores_1_r7, registradores_1_r8,
       registradores_1_r9, registradores_1_r10, registradores_1_r11, registradores_1_r12,
       registradores_1_r13, registradores_1_ra_2, registradores_1_sp_2;

  Decoder #(.select(4)) decoder_1 (
    .out0(decoder_1_out0), .out1(decoder_1_out1), .out2(decoder_1_out2), .out3(decoder_1_out3),
    .out4(decoder_1_out4), .out5(decoder_1_out5), .out6(decoder_1_out6), .out7(decoder_1_out7),
    .out8(decoder_1_out8), .out9(decoder_1_out9), .out10(decoder_1_out10), .out11(decoder_1_out11),
    .out12(decoder_1_out12), .out13(decoder_1_out13), .out14(decoder_1_out14), .out15(decoder_1_out15),
    .sel(RD));  // open: en
  registradores registradores_1 (
    .Load(Load), .en0(decoder_1_out0), .en1(decoder_1_out1), .en2(decoder_1_out2), .en3(decoder_1_out3),
    .en4(decoder_1_out4), .en5(decoder_1_out5), .en6(decoder_1_out6), .en7(decoder_1_out7),
    .en8(decoder_1_out8), .en9(decoder_1_out9), .en10(decoder_1_out10), .en11(decoder_1_out11),
    .en12(decoder_1_out12), .en13(decoder_1_out13), .SP(decoder_1_out14), .RA(decoder_1_out15),
    .WriteEnable(RegWrite), .clk(clk), .R0(registradores_1_r0), .R1(registradores_1_r1),
    .R2(registradores_1_r2), .R3(registradores_1_r3), .R4(registradores_1_r4), .R5(registradores_1_r5),
    .R6(registradores_1_r6), .R7(registradores_1_r7), .R8(registradores_1_r8), .R9(registradores_1_r9),
    .R10(registradores_1_r10), .R11(registradores_1_r11), .R12(registradores_1_r12),
    .R13(registradores_1_r13), .SP_2(registradores_1_sp_2), .RA_2(registradores_1_ra_2));
  Multiplexer #(.select(4), .width(4)) multiplexer_1 (
    .in0(registradores_1_r0), .in1(registradores_1_r1), .in2(registradores_1_r2), .in3(registradores_1_r3),
    .in4(registradores_1_r4), .in5(registradores_1_r5), .in6(registradores_1_r6), .in7(registradores_1_r7),
    .in8(registradores_1_r8), .in9(registradores_1_r9), .in10(registradores_1_r10),
    .in11(registradores_1_r11), .in12(registradores_1_r12), .in13(registradores_1_r13),
    .in14(registradores_1_sp_2), .in15(registradores_1_ra_2), .out(Register_Out), .sel(r1_ad));  // open: en
endmodule

module Timing_and_Control (
  input  [3:0] Imediato,
  input  Seletor_PC,
  input  PC_Load,
  input  clk,
  output [3:0] PC
);

  wire [3:0] adder_2_out, multiplexer_1_out, PC_1, ULA;

  Adder #(.width(4)) adder_1 (.a(PC), .b(4'b0001), .out(PC_1));  // open: cin, cout
  Adder #(.width(4)) adder_2 (.a(PC), .b(Imediato), .out(adder_2_out));  // open: cin, cout
  Multiplexer #(.select(2), .width(4)) multiplexer_1 (
    .in1(PC_1), .in2(adder_2_out), .in3(ULA), .out(multiplexer_1_out), .en(Seletor_PC));  // open: in0, sel
  Register #(.width(4)) u_PC (.D(multiplexer_1_out), .en(PC_Load), .Q(PC), .clk(clk));  // open: clr

  // Notes on the sheet:
  //   Q: Precisa de saída PC+1
  //   Q: Precisa de conexão com ULA?
  //   PC_SELECT
endmodule

module Unidade_Controle (
  input  Clock,
  input  Reset,
  input  [7:0] Opcode,
  input  Zero_Flag,
  input  Carry_Flag,
  output Mem_Read,
  output Mem_Write,
  output Mem_Data_Src,
  output [1:0] Addr_Src,
  output IR_Write,
  output Reg_Write,
  output Reg_Src,
  output ACC_Write,
  output [1:0] ACC_Src,
  output Carry_Write,
  output Flag_Sel,
  output PC_Write,
  output [1:0] PC_Src,
  output [2:0] ALU_Op,
  output ALU_SrcB,
  output SP_Update,
  output IMM_Write
);

  wire [1:0] SelectMux;
  wire [4:0] adder_1_out, multiplexer_1_out, rom_1_data, STATE_ID;

  Adder #(.width(5)) adder_1 (.a(STATE_ID), .b(5'b00001), .out(adder_1_out));  // open: cin, cout
  ROM #(.dataWidth(5)) rom_1 (.addr(Opcode), .data(rom_1_data));  // open: sel
  ROM #(.addrWidth(5), .dataWidth(24)) rom_2 (
    .addr(STATE_ID),
    .data({SelectMux, IMM_Write, SP_Update, ALU_SrcB, ALU_Op, PC_Src, PC_Write, Flag_Sel, Carry_Write, ACC_Src, ACC_Write, Reg_Src, Reg_Write, IR_Write, Addr_Src, Mem_Data_Src, Mem_Write, Mem_Read}));  // open: sel
  Multiplexer #(.select(2), .width(5)) multiplexer_1 (
    .in0({5{1'b0}}), .in1(adder_1_out), .in2(rom_1_data), .out(multiplexer_1_out), .sel(SelectMux));  // open: in3, en
  Register #(.width(5)) REGISTRADOR_DE_ESTADO (
    .D(multiplexer_1_out), .Q(STATE_ID), .clk(Clock), .clr(Reset));  // open: en

  // Notes on the sheet:
  //   DECODER ROM
  //   ROM DE SAÍDA
  //   contents of rom_2 (hex, n*v repeats v):
  //   20111 40000 0 40
endmodule

module Unidade_Controle2 (
  input  Clock,
  input  [4:0] Opcode,
  input  Reset,
  output Carry_Write,
  output [2:0] ALU_Op,
  output [2:0] MUX_ACC_Sel,
  output ACC_Write,
  output MUX_In_De_Sel,
  output MUX_Reg_Data_Sel,
  output RegWrite,
  output [1:0] MUX_Addr_Sel,
  output MemWrite,
  output MemRead,
  output IR_Write,
  output [1:0] MUX_PC_Sel,
  output PC_Write,
  output Branch,
  output MUX_Flag_Sel,
  output MUX_RAM_Sel,
  output fib_N__Write
);

  wire not_1_out;
  wire [2:0] counter_1_q;
  wire [19:19] rom_1_data;

  Counter #(.width(3), .max('h7)) counter_1 (
    .load(rom_1_data[19]), .D(3'b000), .count(not_1_out), .Q(counter_1_q), .clk(Clock), .clr(Reset));  // open: carry
  not not_1 (not_1_out, rom_1_data[19]);
  ROM #(.dataWidth(24)) rom_1 (
    .addr({Opcode, counter_1_q}),
    .data({fib_N__Write, MUX_RAM_Sel, MUX_Flag_Sel, Branch, rom_1_data[19], PC_Write, MUX_PC_Sel, IR_Write, MemRead, MemWrite, MUX_Addr_Sel, RegWrite, MUX_Reg_Data_Sel, MUX_In_De_Sel, ACC_Write, MUX_ACC_Sel, ALU_Op, Carry_Write}));  // open: sel

  // Notes on the sheet:
  //   Reset
  //   contents of rom_1 (hex, n*v repeats v):
  //   4c000 800c0 6*0 4c000 800a0 6*0 4c000 800b0 6*0 4c000 80400 6*0 4c000 80081 6*0 4c000 80083 6*0
  //   4c000 400 83000 5*0 4c000 5090 500 80400 4*0 4c000 400 403000 d0000 4*0 4c000 5000 500 e0000 4*0
  //   4c000 44000 d0000 5*0 4c000 44000 1d0000 5*0 4c000 44000 3c0000 5*0 4c000 82800 6*0 4c000 84890 6*0
  //   4c000 880000 6*0 4c000 80409 6*0 4c000 8040a 6*0 4c000 7*0 4c000 7*0 4c000 7*0 4c000 7*0 4c000 7*0
  //   4c000 7*0 4c000 7*0 4c000 7*0 4c000 7*0 4c000 7*0 4c000 7*0 4c000 7*0 4c000 7*0 4c000
endmodule
